// Logisim project Tic-Tac-Toe.circ as structural Verilog: 12 circuits, main circuit main
module main (
);

  wire and_3_out, and_4_out, and_5_out, B1, B2, B3, B4, B5, B6, B7, B8, B9, button_1_out, cdm_8_1_p2,
       cdm_8_1_p4, cdm_8_1_p5, cdm_8_1_p6, cdm_8_1_p7, cdm_8_1_p8, cdm_8_1_p9, cdm_8_1_p10, cdm_8_1_p11, cl,
       code, data, I_Osel, in_out, nand_1_out, nor_1_out, nor_2_out, not_1_out, not_2_out, not_3_out,
       not_4_out, not_5_out, not_7_out, not_8_out, RAM, rs_latch_1_q_prime, transistor_1_out;
  wire [3:0] controlled_buffer_3_out, displayreg1_1_value, displayreg2_1_value, displayreg3_1_value,
       displayreg4_1_value, displayreg5_1_value, displayreg6_1_value, displayreg7_1_value,
       displayreg8_1_value, displayreg9_1_value, I_Oadr, pull_resistor_11_node, random_1_out, register_1_q;
  wire [7:0] cdm_8_1_p14, cdm_8_1_p15, I_Odat;
  wire [7:4] cdm_8_1_p13;
  wire [7:7] not_6_out;
  wire [8:0] _11, _12, _13, _14, _15, _21, _22, _23, _24, _25, _31, _32, _33, _34, _35, _41, _42, _43, _44,
       _45, _51, _52, _53, _54, _55, _61, _62, _63, _64, _65, _71, _72, _73, _74, _75, _81, _82, _83, _84,
       _85, _91, _92, _93, _94, _95;

  // Probe on cdm_8_1_p2
  Button button_1 (.out(button_1_out));
  Clock clock_1 (.out(cl));
  and and_1 (I_Osel, not_1_out, cl, data);
  DotMatrix #(.matrixcols(9), .matrixrows(9)) dotmatrix_1 (
    .col0(_11), .col1(_12), .col2(_13), .col3(_14), .col4(_15), .col5(_14), .col6(_13), .col7(_12), .col8(_11));
  DotMatrix #(.matrixcols(9), .matrixrows(9)) dotmatrix_2 (
    .col0(_41), .col1(_42), .col2(_43), .col3(_44), .col4(_45), .col5(_44), .col6(_43), .col7(_42), .col8(_41));
  DotMatrix #(.matrixcols(9), .matrixrows(9)) dotmatrix_3 (
    .col0(_71), .col1(_72), .col2(_73), .col3(_74), .col4(_75), .col5(_74), .col6(_73), .col7(_72), .col8(_71));
  // Probe on cdm_8_1_p5
  // Probe on cdm_8_1_p6
  // Probe on cdm_8_1_p4
  not not_1 (not_1_out, nand_1_out);
  // Probe on cdm_8_1_p8
  // Probe on cdm_8_1_p9
  // Probe on cdm_8_1_p7
  nand nand_1 (nand_1_out, cdm_8_1_p13[4], cdm_8_1_p13[5], cdm_8_1_p13[6], cdm_8_1_p13[7]);
  and and_2 (RAM, nand_1_out, data);
  DotMatrix #(.matrixcols(9), .matrixrows(9)) dotmatrix_4 (
    .col0(_21), .col1(_22), .col2(_23), .col3(_24), .col4(_25), .col5(_24), .col6(_23), .col7(_22), .col8(_21));
  DotMatrix #(.matrixcols(9), .matrixrows(9)) dotmatrix_5 (
    .col0(_51), .col1(_52), .col2(_53), .col3(_54), .col4(_55), .col5(_54), .col6(_53), .col7(_52), .col8(_51));
  DotMatrix #(.matrixcols(9), .matrixrows(9)) dotmatrix_6 (
    .col0(_81), .col1(_82), .col2(_83), .col3(_84), .col4(_85), .col5(_84), .col6(_83), .col7(_82), .col8(_81));
  Decoder #(.disabled(0)) decoder_1 (.out0(code), .out1(data), .sel(cdm_8_1_p10), .en(cdm_8_1_p11));
  // CdM_8 cdm_8_1: pin names not known; wires that end beside it: cl, cdm_8_1_p2, button_1_out, cdm_8_1_p4, cdm_8_1_p5, cdm_8_1_p6, cdm_8_1_p7, cdm_8_1_p8, cdm_8_1_p9, cdm_8_1_p10, cdm_8_1_p11, in_out, {cdm_8_1_p13, I_Oadr}, cdm_8_1_p14, cdm_8_1_p15
  assign cdm_8_1_p15 = in_out ? I_Odat : 8'bz;  // Controlled_Buffer controlled_buffer_1
  DotMatrix #(.matrixcols(9), .matrixrows(9)) dotmatrix_7 (
    .col0(_31), .col1(_32), .col2(_33), .col3(_34), .col4(_35), .col5(_34), .col6(_33), .col7(_32), .col8(_31));
  DotMatrix #(.matrixcols(9), .matrixrows(9)) dotmatrix_8 (
    .col0(_61), .col1(_62), .col2(_63), .col3(_64), .col4(_65), .col5(_64), .col6(_63), .col7(_62), .col8(_61));
  DotMatrix #(.matrixcols(9), .matrixrows(9)) dotmatrix_9 (
    .col0(_91), .col1(_92), .col2(_93), .col3(_94), .col4(_95), .col5(_94), .col6(_93), .col7(_92), .col8(_91));
  assign I_Odat = not_2_out ? cdm_8_1_p14 : 8'bz;  // Controlled_Buffer controlled_buffer_2
  not not_2 (not_2_out, in_out);
  Pull_Resistor pull_resistor_1 (.node(I_Oadr[0]));
  Pull_Resistor pull_resistor_2 (.node(I_Oadr[1]));
  Pull_Resistor pull_resistor_3 (.node(I_Oadr[2]));
  Pull_Resistor pull_resistor_4 (.node(I_Oadr[3]));
  Pull_Resistor pull_resistor_5 (.node(cdm_8_1_p13[4]));
  Pull_Resistor pull_resistor_6 (.node(cdm_8_1_p13[5]));
  Pull_Resistor pull_resistor_7 (.node(cdm_8_1_p13[6]));
  Pull_Resistor pull_resistor_8 (.node(cdm_8_1_p13[7]));
  ROM rom_1 (.addr({cdm_8_1_p13, I_Oadr}), .data(I_Odat), .sel(code));
  RAM ram_1 (.addr({cdm_8_1_p13, I_Oadr}), .data(I_Odat), .sel(RAM), .clk(cl), .ld(in_out));  // open: clr
  Pull_Resistor pull_resistor_9 (.node(I_Odat));
  Button button_2 (.out(B2));
  Button button_3 (.out(B1));
  Button button_4 (.out(B4));
  Button button_5 (.out(B5));
  Button button_6 (.out(B8));
  Button button_7 (.out(B7));
  DisplayReg1 displayreg1_1 (
    .in_out(in_out), .I_Odat(I_Odat[3:0]), .value(displayreg1_1_value), .I_Oadr(I_Oadr), .I_Osel(I_Osel),
    .out(I_Odat[3:0]));
  Button button_8 (.out(B3));
  Button button_9 (.out(B6));
  Button button_10 (.out(B9));
  DisplayReg2 displayreg2_1 (
    .in_out(in_out), .I_Odat(I_Odat[3:0]), .value(displayreg2_1_value), .I_Oadr(I_Oadr), .I_Osel(I_Osel),
    .out(I_Odat[3:0]));
  not not_3 (not_3_out, transistor_1_out);
  DisplayReg3 displayreg3_1 (
    .in_out(in_out), .I_Odat(I_Odat[3:0]), .value(displayreg3_1_value), .I_Oadr(I_Oadr), .I_Osel(I_Osel),
    .out(I_Odat[3:0]));
  DisplayReg4 displayreg4_1 (
    .in_out(in_out), .I_Odat(I_Odat[3:0]), .value(displayreg4_1_value), .I_Oadr(I_Oadr), .I_Osel(I_Osel),
    .out(I_Odat[3:0]));
  DisplayControl displaycontrol_1 (
    .\input (displayreg2_1_value), .outSignals_1_2({_22, _21}), .outSignals_3_4_5({_25, _24, _23}));
  DisplayControl displaycontrol_2 (
    .\input (displayreg1_1_value), .outSignals_1_2({_12, _11}), .outSignals_3_4_5({_15, _14, _13}));
  Transistor #(.\type ("n")) transistor_1 (.in(1'b0), .out(transistor_1_out), .gate(B1));
  assign controlled_buffer_3_out = B1 ? 4'b0001 : 4'bz;  // Controlled_Buffer controlled_buffer_3
  assign controlled_buffer_3_out = B2 ? 4'b0010 : 4'bz;  // Controlled_Buffer controlled_buffer_4
  DisplayReg5 displayreg5_1 (
    .in_out(in_out), .I_Odat(I_Odat[3:0]), .value(displayreg5_1_value), .I_Oadr(I_Oadr), .I_Osel(I_Osel),
    .out(I_Odat[3:0]));
  DisplayControl displaycontrol_3 (
    .\input (displayreg4_1_value), .outSignals_1_2({_42, _41}), .outSignals_3_4_5({_45, _44, _43}));
  DisplayControl displaycontrol_4 (
    .\input (displayreg3_1_value), .outSignals_1_2({_32, _31}), .outSignals_3_4_5({_35, _34, _33}));
  DisplayControl displaycontrol_5 (
    .\input (displayreg5_1_value), .outSignals_1_2({_52, _51}), .outSignals_3_4_5({_55, _54, _53}));
  Transistor #(.\type ("n")) transistor_2 (.in(1'b0), .out(transistor_1_out), .gate(B3));
  Transistor #(.\type ("n")) transistor_3 (.in(1'b0), .out(transistor_1_out), .gate(B2));
  assign controlled_buffer_3_out = B3 ? 4'b0011 : 4'bz;  // Controlled_Buffer controlled_buffer_5
  assign controlled_buffer_3_out = B4 ? 4'b0100 : 4'bz;  // Controlled_Buffer controlled_buffer_6
  nor nor_1 (nor_1_out, not_3_out, not_4_out);
  not not_4 (not_4_out, not_3_out);
  nor nor_2 (nor_2_out, and_5_out, not_5_out);
  not not_5 (not_5_out, and_5_out);
  DisplayReg6 displayreg6_1 (
    .in_out(in_out), .I_Odat(I_Odat[3:0]), .value(displayreg6_1_value), .I_Oadr(I_Oadr), .I_Osel(I_Osel),
    .out(I_Odat[3:0]));
  DisplayControl displaycontrol_6 (
    .\input (displayreg6_1_value), .outSignals_1_2({_62, _61}), .outSignals_3_4_5({_65, _64, _63}));
  DisplayControl displaycontrol_7 (
    .\input (displayreg8_1_value), .outSignals_1_2({_82, _81}), .outSignals_3_4_5({_85, _84, _83}));
  DisplayControl displaycontrol_8 (
    .\input (displayreg7_1_value), .outSignals_1_2({_72, _71}), .outSignals_3_4_5({_75, _74, _73}));
  Transistor #(.\type ("n")) transistor_4 (.in(1'b0), .out(transistor_1_out), .gate(B5));
  Transistor #(.\type ("n")) transistor_5 (.in(1'b0), .out(transistor_1_out), .gate(B4));
  assign controlled_buffer_3_out = B6 ? 4'b0110 : 4'bz;  // Controlled_Buffer controlled_buffer_7
  assign controlled_buffer_3_out = B5 ? 4'b0101 : 4'bz;  // Controlled_Buffer controlled_buffer_8
  RS_latch rs_latch_1 (.S(nor_1_out), .R(nor_2_out), .Q_prime(rs_latch_1_q_prime));  // open: Q, reset
  DisplayReg7 displayreg7_1 (
    .in_out(in_out), .I_Odat(I_Odat[3:0]), .value(displayreg7_1_value), .I_Oadr(I_Oadr), .I_Osel(I_Osel),
    .out(I_Odat[3:0]));
  DisplayReg8 displayreg8_1 (
    .in_out(in_out), .I_Odat(I_Odat[3:0]), .value(displayreg8_1_value), .I_Oadr(I_Oadr), .I_Osel(I_Osel),
    .out(I_Odat[3:0]));
  DisplayControl displaycontrol_9 (
    .\input (displayreg9_1_value), .outSignals_1_2({_92, _91}), .outSignals_3_4_5({_95, _94, _93}));
  Transistor #(.\type ("n")) transistor_6 (.in(1'b0), .out(transistor_1_out), .gate(B6));
  Transistor #(.\type ("n")) transistor_7 (.in(1'b0), .out(transistor_1_out), .gate(B7));
  assign controlled_buffer_3_out = B7 ? 4'b0111 : 4'bz;  // Controlled_Buffer controlled_buffer_9
  assign controlled_buffer_3_out = B8 ? 4'b1000 : 4'bz;  // Controlled_Buffer controlled_buffer_10
  not not_6 (not_6_out[7], rs_latch_1_q_prime);
  DisplayReg9 displayreg9_1 (
    .in_out(in_out), .I_Odat(I_Odat[3:0]), .value(displayreg9_1_value), .I_Oadr(I_Oadr), .I_Osel(I_Osel),
    .out(I_Odat[3:0]));
  Pull_Resistor #(.pull(1)) pull_resistor_10 (.node(transistor_1_out));
  Transistor #(.\type ("n")) transistor_8 (.in(1'b0), .out(transistor_1_out), .gate(B9));
  Transistor #(.\type ("n")) transistor_9 (.in(1'b0), .out(transistor_1_out), .gate(B8));
  assign controlled_buffer_3_out = B9 ? 4'b1001 : 4'bz;  // Controlled_Buffer controlled_buffer_11
  Pull_Resistor pull_resistor_11 (.node(pull_resistor_11_node));
  not not_7 (not_7_out, not_8_out);
  not not_8 (not_8_out, transistor_1_out);
  Register #(.width(4), .trigger("falling")) register_1 (
    .D(controlled_buffer_3_out), .Q(register_1_q), .clk(not_7_out));  // open: en, clr
  assign I_Odat = and_5_out ? {{4{not_6_out[7]}}, register_1_q} : 8'bz;  // Controlled_Buffer controlled_buffer_12
  and and_3 (and_3_out, I_Osel, I_Oadr[0], I_Oadr[1], ~I_Oadr[2], I_Oadr[3], in_out);  // AND_Gate
  Random #(.width(4), .seed(123)) random_1 (.clk(cl), .out(random_1_out));  // open: next, clr
  assign I_Odat[3:0] = and_3_out ? random_1_out : 4'bz;  // Controlled_Buffer controlled_buffer_13
  assign I_Odat[7:4] = and_3_out ? 4'b0000 : 4'bz;  // Controlled_Buffer controlled_buffer_14
  and and_4 (and_4_out, ~I_Oadr[0], I_Oadr[1], ~I_Oadr[2], I_Oadr[3], I_Osel);  // AND_Gate
  and and_5 (and_5_out, and_4_out, in_out);

  // Other names for the same wires on the sheet: rd_rw = in_out

  // Notes on the sheet:
  //   contents of rom_1 (hex, n*v repeats v):
  //   d0 fa b1 5 e5 2 b7 f e1 0 d2 3 a6 d0 fb b2 d3 9 7e e4 d a ed d d3 f0 5e bb f e1 d d3 2 ab ee 0 d4
  //   2
  //   1
  //   Input controller
  //   5
  //   3
  //   4
  //   I/O Adr: 11110001
  //   7
  //   6
  //   8
  //   9
  //   I/O Adr: 11110010
  //   Screen data setters
  //   Screen choosers
endmodule

module DisplayControl (
  input  [3:0] \input ,
  output [17:0] outSignals_1_2,
  output [26:0] outSignals_3_4_5
);

  Multiplexer #(.width(18), .disabled(0)) multiplexer_1 (
    .in0(18'h202fe), .in1(18'h10501), .out(outSignals_1_2), .sel(\input [0]), .en(\input [1]));
  Pull_Resistor pull_resistor_1 (.node(outSignals_1_2));
  Multiplexer #(.width(27), .disabled(0)) multiplexer_2 (
    .in0(27'h4060301), .in1(27'h405044), .out(outSignals_3_4_5), .sel(\input [0]), .en(\input [1]));
  Pull_Resistor pull_resistor_2 (.node(outSignals_3_4_5));
endmodule

module DisplayReg1 (
  input  I_Osel,
  input  [3:0] I_Oadr,
  input  in_out,
  input  [3:0] I_Odat,
  output [3:0] out,
  output [3:0] value
);

  wire and_1_out, decoder_1_out0, decoder_1_out1;

  Register #(.width(4)) register_1 (.D(I_Odat), .Q(value), .clk(decoder_1_out0));  // open: en, clr
  assign out = decoder_1_out1 ? value : 4'bz;  // Controlled_Buffer controlled_buffer_1
  and and_1 (and_1_out, ~I_Oadr[3], ~I_Oadr[2], ~I_Oadr[1], I_Oadr[0], I_Osel);  // AND_Gate
  Decoder #(.disabled(0)) decoder_1 (.out0(decoder_1_out0), .out1(decoder_1_out1), .sel(in_out), .en(and_1_out));
endmodule

module DisplayReg2 (
  input  I_Osel,
  input  [3:0] I_Oadr,
  input  in_out,
  input  [3:0] I_Odat,
  output [3:0] out,
  output [3:0] value
);

  wire and_1_out, decoder_1_out0, decoder_1_out1;

  Register #(.width(4)) register_1 (.D(I_Odat), .Q(value), .clk(decoder_1_out0));  // open: en, clr
  assign out = decoder_1_out1 ? value : 4'bz;  // Controlled_Buffer controlled_buffer_1
  and and_1 (and_1_out, ~I_Oadr[3], ~I_Oadr[2], I_Oadr[1], ~I_Oadr[0], I_Osel);  // AND_Gate
  Decoder #(.disabled(0)) decoder_1 (.out0(decoder_1_out0), .out1(decoder_1_out1), .sel(in_out), .en(and_1_out));
endmodule

module DisplayReg3 (
  input  I_Osel,
  input  [3:0] I_Oadr,
  input  in_out,
  input  [3:0] I_Odat,
  output [3:0] out,
  output [3:0] value
);

  wire and_1_out, decoder_1_out0, decoder_1_out1;

  Register #(.width(4)) register_1 (.D(I_Odat), .Q(value), .clk(decoder_1_out0));  // open: en, clr
  assign out = decoder_1_out1 ? value : 4'bz;  // Controlled_Buffer controlled_buffer_1
  and and_1 (and_1_out, ~I_Oadr[3], ~I_Oadr[2], I_Oadr[1], I_Oadr[0], I_Osel);  // AND_Gate
  Decoder #(.disabled(0)) decoder_1 (.out0(decoder_1_out0), .out1(decoder_1_out1), .sel(in_out), .en(and_1_out));
endmodule

module DisplayReg4 (
  input  I_Osel,
  input  [3:0] I_Oadr,
  input  in_out,
  input  [3:0] I_Odat,
  output [3:0] out,
  output [3:0] value
);

  wire and_1_out, decoder_1_out0, decoder_1_out1;

  Register #(.width(4)) register_1 (.D(I_Odat), .Q(value), .clk(decoder_1_out0));  // open: en, clr
  assign out = decoder_1_out1 ? value : 4'bz;  // Controlled_Buffer controlled_buffer_1
  and and_1 (and_1_out, ~I_Oadr[3], I_Oadr[2], ~I_Oadr[1], ~I_Oadr[0], I_Osel);  // AND_Gate
  Decoder #(.disabled(0)) decoder_1 (.out0(decoder_1_out0), .out1(decoder_1_out1), .sel(in_out), .en(and_1_out));
endmodule

module DisplayReg5 (
  input  I_Osel,
  input  [3:0] I_Oadr,
  input  in_out,
  input  [3:0] I_Odat,
  output [3:0] out,
  output [3:0] value
);

  wire and_1_out, decoder_1_out0, decoder_1_out1;

  Register #(.width(4)) register_1 (.D(I_Odat), .Q(value), .clk(decoder_1_out0));  // open: en, clr
  assign out = decoder_1_out1 ? value : 4'bz;  // Controlled_Buffer controlled_buffer_1
  and and_1 (and_1_out, ~I_Oadr[3], I_Oadr[2], ~I_Oadr[1], I_Oadr[0], I_Osel);  // AND_Gate
  Decoder #(.disabled(0)) decoder_1 (.out0(decoder_1_out0), .out1(decoder_1_out1), .sel(in_out), .en(and_1_out));
endmodule

module DisplayReg6 (
  input  I_Osel,
  input  [3:0] I_Oadr,
  input  in_out,
  input  [3:0] I_Odat,
  output [3:0] out,
  output [3:0] value
);

  wire and_1_out, decoder_1_out0, decoder_1_out1;

  Register #(.width(4)) register_1 (.D(I_Odat), .Q(value), .clk(decoder_1_out0));  // open: en, clr
  assign out = decoder_1_out1 ? value : 4'bz;  // Controlled_Buffer controlled_buffer_1
  and and_1 (and_1_out, ~I_Oadr[3], I_Oadr[2], I_Oadr[1], ~I_Oadr[0], I_Osel);  // AND_Gate
  Decoder #(.disabled(0)) decoder_1 (.out0(decoder_1_out0), .out1(decoder_1_out1), .sel(in_out), .en(and_1_out));
endmodule

module DisplayReg7 (
  input  I_Osel,
  input  [3:0] I_Oadr,
  input  in_out,
  input  [3:0] I_Odat,
  output [3:0] out,
  output [3:0] value
);

  wire and_1_out, decoder_1_out0, decoder_1_out1;

  Register #(.width(4)) register_1 (.D(I_Odat), .Q(value), .clk(decoder_1_out0));  // open: en, clr
  assign out = decoder_1_out1 ? value : 4'bz;  // Controlled_Buffer controlled_buffer_1
  and and_1 (and_1_out, ~I_Oadr[3], I_Oadr[2], I_Oadr[1], I_Oadr[0], I_Osel);  // AND_Gate
  Decoder #(.disabled(0)) decoder_1 (.out0(decoder_1_out0), .out1(decoder_1_out1), .sel(in_out), .en(and_1_out));
endmodule

module DisplayReg8 (
  input  I_Osel,
  input  [3:0] I_Oadr,
  input  in_out,
  input  [3:0] I_Odat,
  output [3:0] out,
  output [3:0] value
);

  wire and_1_out, decoder_1_out0, decoder_1_out1;

  Register #(.width(4)) register_1 (.D(I_Odat), .Q(value), .clk(decoder_1_out0));  // open: en, clr
  assign out = decoder_1_out1 ? value : 4'bz;  // Controlled_Buffer controlled_buffer_1
  and and_1 (and_1_out, I_Oadr[3], ~I_Oadr[2], ~I_Oadr[1], ~I_Oadr[0], I_Osel);  // AND_Gate
  Decoder #(.disabled(0)) decoder_1 (.out0(decoder_1_out0), .out1(decoder_1_out1), .sel(in_out), .en(and_1_out));
endmodule

module DisplayReg9 (
  input  I_Osel,
  input  [3:0] I_Oadr,
  input  in_out,
  input  [3:0] I_Odat,
  output [3:0] out,
  output [3:0] value
);

  wire and_1_out, decoder_1_out0, decoder_1_out1;

  Register #(.width(4)) register_1 (.D(I_Odat), .Q(value), .clk(decoder_1_out0));  // open: en, clr
  assign out = decoder_1_out1 ? value : 4'bz;  // Controlled_Buffer controlled_buffer_1
  and and_1 (and_1_out, I_Oadr[3], ~I_Oadr[2], ~I_Oadr[1], I_Oadr[0], I_Osel);  // AND_Gate
  Decoder #(.disabled(0)) decoder_1 (.out0(decoder_1_out0), .out1(decoder_1_out1), .sel(in_out), .en(and_1_out));
endmodule

module RS (
  input  S,
  input  R,
  output Q_prime,
  output Q
);

  wire or_1_out, transistor_1_out, transistor_2_out, transistor_3_out;

  Transistor transistor_1 (.in(1'b1), .out(transistor_1_out), .gate(R));
  Transistor #(.\type ("n"), .gate("br")) transistor_2 (.in(1'b0), .out(transistor_2_out), .gate(R));
  Transistor #(.\type ("n")) transistor_3 (.in(transistor_1_out), .out(transistor_3_out), .gate(S));
  Pull_Resistor #(.pull(1)) pull_resistor_1 (.node(transistor_3_out));
  Transistor #(.gate("br")) transistor_4 (.in(transistor_2_out), .out(transistor_3_out), .gate(S));
  Register #(.width(1), .trigger("high")) register_1 (.D(transistor_3_out), .Q(Q), .clk(or_1_out));  // open: en, clr
  or or_1 (or_1_out, S, R);
  not not_1 (Q_prime, Q);
endmodule
